// Logisim project Circuito simplificado - TP1 ISL.circ as structural Verilog: 1 circuit, main circuit main
module main (
  input  A,
  input  B,
  input  C,
  input  D,
  output out_5,
  output out_6,
  output out_7,
  output out_8
);

  wire and_1_out, and_2_out, and_3_out, and_4_out, and_5_out, and_6_out, and_7_out, and_8_out, and_9_out,
       and_10_out, and_11_out, and_12_out, and_13_out, and_14_out, and_15_out, and_16_out, not_1_out,
       not_2_out, not_3_out, not_4_out, or_5_out, or_6_out, or_7_out, or_8_out;

  and and_1 (and_1_out, C, D);
  and and_2 (and_2_out, ~A, ~B, ~C);  // AND_Gate
  and and_3 (and_3_out, C, ~A, B);  // AND_Gate
  and and_4 (and_4_out, C, ~B, A);  // AND_Gate
  and and_5 (and_5_out, ~A, C);  // AND_Gate
  and and_6 (and_6_out, B, C);
  and and_7 (and_7_out, ~A, B, ~D);  // AND_Gate
  and and_8 (and_8_out, A, ~B, ~C, ~D);  // AND_Gate
  and and_9 (and_9_out, ~B, ~C, ~D);  // AND_Gate
  and and_10 (and_10_out, ~A, ~B, ~D);  // AND_Gate
  and and_11 (and_11_out, C, ~A, D);  // AND_Gate
  and and_12 (and_12_out, D, ~B, C);  // AND_Gate
  and and_13 (and_13_out, B, ~C, D);  // AND_Gate
  and and_14 (and_14_out, ~C, ~D);  // AND_Gate
  and and_15 (and_15_out, ~B, D, ~A);  // AND_Gate
  and and_16 (and_16_out, A, B, D);
  or or_1 (out_5, and_1_out, and_2_out, and_3_out, and_4_out);
  or or_2 (out_6, and_5_out, and_6_out, and_7_out, and_8_out);
  or or_3 (out_7, and_9_out, and_10_out, and_11_out, and_12_out, and_13_out);
  or or_4 (out_8, and_14_out, and_15_out, and_16_out);
  not not_1 (not_1_out, out_5);
  not not_2 (not_2_out, out_6);
  not not_3 (not_3_out, out_7);
  not not_4 (not_4_out, out_8);
  _7_Segment_Display u_7_segment_display_1 (
    .f(not_1_out), .a(not_1_out), .b(or_5_out), .e(not_1_out), .d(not_1_out), .c(or_5_out));  // open: g, dp
  or or_5 (or_5_out, not_1_out, out_5);
  _7_Segment_Display u_7_segment_display_2 (
    .f(not_2_out), .a(not_2_out), .b(or_6_out), .e(not_2_out), .d(not_2_out), .c(or_6_out));  // open: g, dp
  or or_6 (or_6_out, not_2_out, out_6);
  _7_Segment_Display u_7_segment_display_3 (
    .f(not_3_out), .a(not_3_out), .b(or_7_out), .e(not_3_out), .d(not_3_out), .c(or_7_out));  // open: g, dp
  or or_7 (or_7_out, not_3_out, out_7);
  _7_Segment_Display u_7_segment_display_4 (
    .f(not_4_out), .a(not_4_out), .b(or_8_out), .e(not_4_out), .d(not_4_out), .c(or_8_out));  // open: g, dp
  or or_8 (or_8_out, not_4_out, out_8);

  // Notes on the sheet:
  //   S2
  //   S3
  //   S1
  //   SO
endmodule
